# Fritzing sketch current-measurement (saved by Fritzing 0.8.5b)
breadboards: 1

parts:
  ACS712ELCTR-20A = ACS712 Low Current Sensor Board v12
  HJ_S3315D = Basic Servo

nets:
  7.15V: ACS712ELCTR-20A.IP+
  N1: ACS712ELCTR-20A.IP-, HJ_S3315D.vcc
  5V: ACS712ELCTR-20A.5V
  GND: ACS712ELCTR-20A.GND, HJ_S3315D.gnd

notes:
  Arbotix Analog In Pin
  Arduino PWM Signal
  For Current Measurement
